// Logisim project cpu.circ as structural Verilog: 19 circuits, main circuit COMPUTER
module ALU (
  input  [7:0] in_1,
  input  [31:0] in_2,
  input  [31:0] in_3,
  output [31:0] ALU
);

  wire [3:0] bit_extender_1_out;
  wire [31:0] adder_1_out, adder_2_out, adder_3_out, and_1_out, divider_1_out, divider_1_rem,
       multiplier_1_out, multiplier_2_out, not_1_out, or_1_out, subtractor_1_out;

  Bit_Extender #(.out_width(4)) bit_extender_1 (.in(in_1), .out(bit_extender_1_out));
  assign and_1_out = in_2 & in_3;  // AND_Gate and_1, 32 bits wide
  assign or_1_out = in_2 | in_3;  // OR_Gate or_1, 32 bits wide
  assign not_1_out = ~in_2;  // NOT_Gate not_1, 32 bits wide
  Adder #(.width(32)) adder_1 (.a(in_2), .b(in_3), .out(adder_1_out));  // open: cin, cout
  Subtractor #(.width(32)) subtractor_1 (.a(in_2), .b(in_3), .out(subtractor_1_out));  // open: bin, bout
  Multiplier #(.width(32)) multiplier_1 (.a(in_2), .b(in_3), .out(multiplier_1_out));  // open: cin, cout
  Divider #(.width(32)) divider_1 (.a(in_2), .b(in_3), .out(divider_1_out), .rem(divider_1_rem));  // open: upper
  Multiplier #(.width(32)) multiplier_2 (.a(in_2), .b(in_2), .out(multiplier_2_out));  // open: cin, cout
  Adder #(.width(32)) adder_2 (.a(in_2), .b(32'h1), .out(adder_2_out));  // open: cin, cout
  Adder #(.width(32)) adder_3 (.a(in_2), .b(32'h1), .out(adder_3_out));  // open: cin, cout
  Multiplexer #(.select(4), .width(32), .enable("false")) multiplexer_1 (
    .in0({32{1'b0}}), .in1(adder_1_out), .in2(subtractor_1_out), .in3(multiplier_1_out), .in4(divider_1_out),
    .in5(and_1_out), .in6(or_1_out), .in7(not_1_out), .in8(adder_2_out), .in9(adder_3_out),
    .in10(divider_1_rem), .in11(multiplier_2_out), .in12({32{1'b0}}), .in13({32{1'b0}}), .in14({32{1'b0}}),
    .in15({32{1'b0}}), .out(ALU), .sel(bit_extender_1_out));

  // Notes on the sheet:
  //   INS
  //   INPUT A
  //   INPUT B
endmodule

module ACC (
  input  [31:0] INPUT,
  input  ENACC,
  input  CLK,
  output [31:0] ACC
);

  Register #(.width(32)) u_ACC (.D(INPUT), .en(ENACC), .Q(ACC), .clk(CLK));  // open: clr
endmodule

module REGCON (
  input  [31:0] ACC,
  input  [7:0] INS,
  input  ENR,
  input  CLK,
  output [31:0] R0,
  output [31:0] R1,
  output [31:0] R2,
  output [31:0] R3
);

  wire demultiplexer_1_out0, demultiplexer_1_out1, demultiplexer_1_out2, demultiplexer_1_out3, not_1_out;
  wire [1:0] bit_extender_1_out;

  Bit_Extender #(.out_width(2)) bit_extender_1 (.in(INS), .out(bit_extender_1_out));
  Demultiplexer #(.select(2), .enable("false")) demultiplexer_1 (
    .out0(demultiplexer_1_out0), .out1(demultiplexer_1_out1), .out2(demultiplexer_1_out2),
    .out3(demultiplexer_1_out3), .in(ENR), .sel(bit_extender_1_out));
  Register #(.width(32), .trigger("falling")) u_R0 (
    .D(ACC), .en(demultiplexer_1_out0), .Q(R0), .clk(not_1_out));  // open: clr
  Register #(.width(32), .trigger("falling")) u_R1 (
    .D(ACC), .en(demultiplexer_1_out1), .Q(R1), .clk(not_1_out));  // open: clr
  Register #(.width(32), .trigger("falling")) u_R2 (
    .D(ACC), .en(demultiplexer_1_out2), .Q(R2), .clk(not_1_out));  // open: clr
  Register #(.width(32), .trigger("falling")) u_R3 (
    .D(ACC), .en(demultiplexer_1_out3), .Q(R3), .clk(not_1_out));  // open: clr
  not not_1 (not_1_out, CLK);
endmodule

module JMP (
  input  ENJMP,
  input  [7:0] INS,
  input  [31:0] ACC,
  input  [31:0] R0,
  input  [31:0] R1,
  input  [31:0] R2,
  input  [31:0] R3,
  output JMP
);

  wire comparator_1_eq, comparator_2_eq, comparator_2_gt, comparator_2_lt, comparator_3_eq, comparator_3_gt,
       comparator_3_lt, comparator_4_eq, comparator_4_gt, comparator_4_lt, comparator_5_eq, comparator_5_gt,
       comparator_5_lt, multiplexer_1_out, not_1_out;
  wire [3:0] bit_extender_1_out;

  Bit_Extender #(.out_width(4)) bit_extender_1 (.in(INS), .out(bit_extender_1_out));
  Comparator #(.width(32), .mode("unsigned")) comparator_1 (
    .a(ACC), .b({32{1'b0}}), .eq(comparator_1_eq));  // open: gt, lt
  Comparator #(.width(32), .mode("unsigned")) comparator_2 (
    .a(ACC), .b(R0), .gt(comparator_2_gt), .eq(comparator_2_eq), .lt(comparator_2_lt));
  Comparator #(.width(32), .mode("unsigned")) comparator_3 (
    .a(ACC), .b(R1), .gt(comparator_3_gt), .eq(comparator_3_eq), .lt(comparator_3_lt));
  Comparator #(.width(32), .mode("unsigned")) comparator_4 (
    .a(ACC), .b(R2), .gt(comparator_4_gt), .eq(comparator_4_eq), .lt(comparator_4_lt));
  Comparator #(.width(32), .mode("unsigned")) comparator_5 (
    .a(ACC), .b(R3), .gt(comparator_5_gt), .eq(comparator_5_eq), .lt(comparator_5_lt));
  and and_1 (JMP, multiplexer_1_out, ENJMP);
  Multiplexer #(.select(4), .disabled(0), .enable("false")) multiplexer_1 (
    .in0(1'b1), .in1(comparator_1_eq), .in2(not_1_out), .in3(comparator_2_eq), .in4(comparator_3_eq),
    .in5(comparator_4_eq), .in6(comparator_5_eq), .in7(comparator_2_lt), .in8(comparator_3_lt),
    .in9(comparator_4_lt), .in10(comparator_5_lt), .in11(comparator_2_gt), .in12(comparator_3_gt),
    .in13(comparator_4_gt), .in14(comparator_5_gt), .in15(1'b0), .out(multiplexer_1_out),
    .sel(bit_extender_1_out));
  not not_1 (not_1_out, comparator_1_eq);
endmodule

module PC (
  input  [31:0] ADRIN,
  input  CLK,
  input  JMP,
  output [23:0] out_4,
  output [23:0] out_5
);

  wire d_ff_1_q, not_1_out;
  wire [23:0] bit_extender_1_out;

  Bit_Extender #(.in_width(32), .out_width(24)) bit_extender_1 (.in(ADRIN), .out(bit_extender_1_out));
  not not_1 (not_1_out, d_ff_1_q);
  D_Flip_Flop #(.trigger("falling")) d_ff_1 (.clk(CLK), .D(JMP), .Q(d_ff_1_q));  // open: Qn, preset, en, reset
  Counter #(.width(24), .max('hffffff)) counter_1 (
    .load(d_ff_1_q), .D(bit_extender_1_out), .count(not_1_out), .Q(out_4), .clk(CLK));  // open: carry, clr

  assign out_5 = out_4;

  // Notes on the sheet:
  //   ADROUT
endmodule

module SELECTOR (
  input  [31:0] REGRAM,
  input  [31:0] REGALU,
  input  [31:0] REGDATA,
  input  [7:0] INS,
  input  [31:0] RAM,
  input  [31:0] ROM,
  input  [31:0] ACC,
  input  [31:0] ALU,
  output [23:0] RAM_2,
  output [31:0] ALU_2,
  output [31:0] out_11,
  output [31:0] out_12
);

  wire [31:0] selram_1_out_5;

  SELRAM selram_1 (.in_3(ROM), .in_2(REGRAM), .in_1(ACC), .in_4(INS), .out_5(selram_1_out_5));
  Bit_Extender #(.in_width(32), .out_width(24)) bit_extender_1 (.in(selram_1_out_5), .out(RAM_2));
  SELALU selalu_1 (.in_3(REGALU), .in_2(ROM), .in_1(RAM), .in_4(INS), .out_5(ALU_2));
  SELDATA seldata_1 (.in_5(ALU), .in_4(REGDATA), .in_3(ACC), .in_2(ROM), .in_1(RAM), .in_6(INS), .out_7(out_11));

  assign out_12 = out_11;

  // Notes on the sheet:
  //   DATA
endmodule

module SELREG (
  input  [7:0] in_1,
  input  [31:0] in_2,
  input  [31:0] in_3,
  input  [31:0] in_4,
  input  [31:0] in_5,
  input  [31:0] in_6,
  output [31:0] out_7,
  output [31:0] out_8,
  output [31:0] out_9
);

  Multiplexer #(.select(2), .width(32), .disabled(0), .enable("false")) multiplexer_1 (
    .in0(in_3), .in1(in_4), .in2(in_5), .in3(in_6), .out(out_7), .sel(in_1[6:5]));
  Multiplexer #(.select(2), .width(32), .enable("false")) multiplexer_2 (
    .in0(in_3), .in1(in_4), .in2(in_5), .in3(in_6), .out(out_8), .sel(in_1[1:0]));
  Multiplexer #(.select(2), .width(32), .enable("false")) multiplexer_3 (
    .in0(in_2), .in1(out_8), .in2(in_2), .in3(out_8), .out(out_9), .sel(in_1[3:2]));

  // Notes on the sheet:
  //   INS
  //   R0
  //   R1
  //   R2
  //   R3
  //   REGALU
  //   REGRAM
  //   REGDATA
  //   ACC
endmodule

module ENABLER (
  input  in_1,
  input  [31:0] ROM,
  input  [31:0] ACC,
  input  [31:0] in_4,
  output out_5,
  output [7:0] out_6,
  output out_7,
  output [31:0] out_8,
  output out_9,
  output [31:0] R0,
  output [31:0] R1,
  output [31:0] out_12,
  output [31:0] REGDATA,
  output [31:0] R2,
  output out_15,
  output [31:0] REGRAM,
  output [31:0] R3,
  output [31:0] REGAULK
);

  wire enjmp_1_ejmp, enr_1_enr, insleng_1_leng;
  wire [7:0] bit_extender_1_out;

  Bit_Extender #(.in_width(32), .out_width(8)) bit_extender_1 (.in(ROM), .out(bit_extender_1_out));
  INSLENG insleng_1 (.CL(in_1), .INVCL(out_9), .INS(out_6), .ROM(bit_extender_1_out), .LENG(insleng_1_leng));
  JMP jmp_1 (.INS(out_6), .R0(R0), .R1(R1), .R2(R2), .R3(R3), .JMP(out_15), .ENJMP(enjmp_1_ejmp), .ACC(ACC));
  SELREG selreg_1 (
    .in_1(out_6), .in_3(R0), .in_4(R1), .in_5(R2), .in_6(R3), .out_7(REGAULK), .out_8(REGRAM),
    .out_9(REGDATA), .in_2(ACC));
  ENRAM enram_1 (.in_1(out_6), .LENG(insleng_1_leng), .ENRAM(out_5));
  ENACC enacc_1 (.in_1(out_6), .LENG(insleng_1_leng), .out_3(out_7));
  ENR enr_1 (.in_1(out_6), .LENG(insleng_1_leng), .ENR(enr_1_enr));
  REGCON regcon_1 (.R0(R0), .R1(R1), .R2(R2), .R3(R3), .ACC(ACC), .INS(out_6), .ENR(enr_1_enr), .CLK(out_9));
  ENJMP enjmp_1 (.LENG(insleng_1_leng), .in_2(out_6), .EJMP(enjmp_1_ejmp));

  assign out_8 = ROM;
  assign out_12 = in_4;

  // Notes on the sheet:
  //   RAM
  //   RAM
  //   INS
endmodule

module INSLENG (
  input  [7:0] ROM,
  input  CL,
  output [7:0] INS,
  output LENG,
  output INVCL
);

  wire controlled_buffer_1_out, D2_q;
  wire [7:0] INS_REG_q;

  not not_1 (INVCL, CL);
  Register INS_REG (.D(ROM), .Q(INS_REG_q), .clk(CL));  // open: en, clr
  D_Flip_Flop D1 (.clk(CL), .D(ROM[4]), .Q(LENG), .reset(controlled_buffer_1_out));  // open: Qn, preset, en
  assign controlled_buffer_1_out = D2_q ? LENG : 1'bz;  // Controlled_Buffer controlled_buffer_1
  D_Flip_Flop D2 (.clk(CL), .D(LENG), .Q(D2_q));  // open: Qn, preset, en, reset
  Multiplexer #(.width(8), .disabled(0), .enable("false")) multiplexer_1 (
    .in0(ROM), .in1(INS_REG_q), .out(INS), .sel(LENG));
endmodule

module ENR (
  input  [7:0] in_1,
  input  LENG,
  output ENR
);

  wire and_2_out, nand_1_out, nor_1_out, not_1_out, or_1_out;

  nor nor_1 (nor_1_out, in_1[2], in_1[3], in_1[4]);
  not not_1 (not_1_out, in_1[4]);
  or or_1 (or_1_out, not_1_out, LENG);
  nand nand_1 (nand_1_out, in_1[6], in_1[7]);
  and and_1 (ENR, nor_1_out, in_1[7], and_2_out);
  and and_2 (and_2_out, or_1_out, nand_1_out);

  // Notes on the sheet:
  //   INS
endmodule

module ENRAM (
  input  [7:0] in_1,
  input  LENG,
  output ENRAM
);

  wire and_1_out, and_2_out, and_3_out, nand_1_out, nor_1_out, not_1_out, or_1_out, or_2_out;

  nor nor_1 (nor_1_out, in_1[0], in_1[1]);
  nand nand_1 (nand_1_out, in_1[6], in_1[7]);
  not not_1 (not_1_out, in_1[4]);
  or or_1 (or_1_out, LENG, not_1_out);
  and and_1 (and_1_out, in_1[3], in_1[7]);
  and and_2 (and_2_out, nor_1_out, in_1[4]);
  and and_3 (and_3_out, nand_1_out, or_1_out);
  or or_2 (or_2_out, and_2_out, and_1_out);
  and and_4 (ENRAM, or_2_out, and_3_out);

  // Notes on the sheet:
  //   INS
endmodule

module ENACC (
  input  [7:0] in_1,
  input  LENG,
  output out_3
);

  wire and_1_out, and_2_out, and_3_out, nand_1_out, not_1_out, not_2_out, not_3_out, or_1_out, or_2_out,
       or_3_out;

  and and_1 (and_1_out, in_1[4], or_1_out);
  or or_1 (or_1_out, in_1[0], in_1[1]);
  and and_2 (and_2_out, in_1[2], not_1_out);
  not not_1 (not_1_out, in_1[3]);
  not not_2 (not_2_out, in_1[7]);
  not not_3 (not_3_out, in_1[4]);
  or or_2 (or_2_out, not_3_out, LENG);
  nand nand_1 (nand_1_out, in_1[6], in_1[7]);
  or or_3 (or_3_out, and_1_out, and_2_out, not_2_out);
  and and_3 (and_3_out, or_2_out, nand_1_out);
  and and_4 (out_3, or_3_out, and_3_out);

  // Notes on the sheet:
  //   INS
endmodule

module ENJMP (
  input  LENG,
  input  [7:0] in_2,
  output EJMP
);

  wire and_1_out, not_1_out, or_1_out;

  not not_1 (not_1_out, in_2[4]);
  and and_1 (and_1_out, in_2[6], in_2[7]);
  or or_1 (or_1_out, LENG, not_1_out);
  and and_2 (EJMP, or_1_out, and_1_out);

  // Notes on the sheet:
  //   INS
endmodule

module CONTROL_UNIT (
  input  [31:0] ROM,
  input  [31:0] RAM_INPUT,
  input  in_3,
  output out_4,
  output out_5,
  output [31:0] R0,
  output [7:0] INS,
  output [31:0] RAM_DATA,
  output [31:0] R1,
  output [23:0] RAM_ADR,
  output [31:0] R2,
  output [31:0] R3,
  output [31:0] ACC,
  output out_14
);

  wire enabler_1_out_7;
  wire [31:0] alu_1_alu, enabler_1_out_8, enabler_1_out_12, enabler_1_regaulk, enabler_1_regdata,
       enabler_1_regram, selector_1_alu_2, selector_1_out_11;

  ENABLER enabler_1 (
    .out_6(INS), .ROM(ROM), .in_1(in_3), .out_15(out_4), .out_5(out_5), .out_7(enabler_1_out_7), .ACC(ACC),
    .out_9(out_14), .R0(R0), .R1(R1), .R2(R2), .R3(R3), .in_4(RAM_INPUT), .out_12(enabler_1_out_12),
    .out_8(enabler_1_out_8), .REGAULK(enabler_1_regaulk), .REGRAM(enabler_1_regram),
    .REGDATA(enabler_1_regdata));
  ACC acc_1 (.INPUT(selector_1_out_11), .ENACC(enabler_1_out_7), .ACC(ACC), .CLK(out_14));
  ALU alu_1 (.in_1(INS), .in_2(ACC), .in_3(selector_1_alu_2), .ALU(alu_1_alu));
  SELECTOR selector_1 (
    .REGRAM(enabler_1_regram), .REGALU(enabler_1_regaulk), .REGDATA(enabler_1_regdata), .ALU(alu_1_alu),
    .ACC(ACC), .ROM(enabler_1_out_8), .RAM(enabler_1_out_12), .INS(INS), .RAM_2(RAM_ADR),
    .ALU_2(selector_1_alu_2), .out_11(selector_1_out_11), .out_12(RAM_DATA));
endmodule

module COMPUTER (
  output [31:0] R0,
  output [31:0] R1,
  output [23:0] PC,
  output [31:0] R2,
  output [31:0] R3,
  output [31:0] ACC
);

  wire clock_1_cl, control_unit_1_out_4, control_unit_1_out_5, control_unit_1_out_14;
  wire [7:0] control_unit_1_ins;
  wire [23:0] control_unit_1_ram_adr, pc_1_out_4;
  wire [31:0] control_unit_1_ram_data, ram_1_data, rom_1_data;

  PC pc_1 (.ADRIN(rom_1_data), .CLK(clock_1_cl), .JMP(control_unit_1_out_4), .out_4(pc_1_out_4), .out_5(PC));
  ROM #(.addrWidth(24), .dataWidth(32)) rom_1 (.addr(pc_1_out_4), .data(rom_1_data));  // open: sel
  CLOCK clock_1 (.INS(control_unit_1_ins), .CL(clock_1_cl));
  CONTROL_UNIT control_unit_1 (
    .RAM_INPUT(ram_1_data), .ROM(rom_1_data), .R0(R0), .R1(R1), .R2(R2), .R3(R3),
    .RAM_DATA(control_unit_1_ram_data), .RAM_ADR(control_unit_1_ram_adr), .out_5(control_unit_1_out_5),
    .out_4(control_unit_1_out_4), .out_14(control_unit_1_out_14), .ACC(ACC), .INS(control_unit_1_ins),
    .in_3(clock_1_cl));
  RAM #(.addrWidth(24), .dataWidth(32), .bus("separate")) ram_1 (
    .addr(control_unit_1_ram_adr), .din(control_unit_1_ram_data), .data(ram_1_data),
    .str(control_unit_1_out_5), .clk(control_unit_1_out_14));  // open: sel, ld, clr

  // Notes on the sheet:
  //   ROM
  //   contents of rom_1 (hex, n*v repeats v):
  //   0 91 1 82 91 4 83 91 1 90 1 92 0 8 90 0 91 0 90 2 92 1 80 92 0 a d2 23 92 2 8 dd 7 90 2 92 0 81 92 1
  //   8 90 1 d8 14 92 0 8b 87 8 83 d0 7
  //   RAM
endmodule

module SELRAM (
  input  [31:0] in_1,
  input  [31:0] in_2,
  input  [31:0] in_3,
  input  [7:0] in_4,
  output [31:0] out_5
);

  Multiplexer #(.select(2), .width(32), .enable("false")) multiplexer_1 (
    .in0(in_3), .in2(in_2), .in3(in_1), .out(out_5), .sel(in_4[3:2]));  // open: in1

  // Notes on the sheet:
  //   ACC
  //   REGRAM
  //   INS
  //   ROM
  //   RAM
endmodule

module SELDATA (
  input  [31:0] in_1,
  input  [31:0] in_2,
  input  [31:0] in_3,
  input  [31:0] in_4,
  input  [31:0] in_5,
  input  [7:0] in_6,
  output [31:0] out_7
);

  wire [31:0] multiplexer_1_out, multiplexer_2_out;

  Multiplexer #(.width(32), .enable("false")) multiplexer_1 (
    .in0(in_4), .in1(multiplexer_2_out), .out(multiplexer_1_out), .sel(in_6[4]));
  Multiplexer #(.select(2), .width(32), .enable("false")) multiplexer_2 (
    .in0(in_3), .in1(in_2), .in2(in_1), .out(multiplexer_2_out), .sel(in_6[1:0]));  // open: in3
  Multiplexer #(.width(32), .enable("false")) multiplexer_3 (
    .in0(in_5), .in1(multiplexer_1_out), .out(out_7), .sel(in_6[7]));

  // Notes on the sheet:
  //   RAM
  //   INS
  //   ROM
  //   ACC
  //   REGDATA
  //   ALU
  //   DATA
endmodule

module SELALU (
  input  [31:0] in_1,
  input  [31:0] in_2,
  input  [31:0] in_3,
  input  [7:0] in_4,
  output [31:0] out_5
);

  Multiplexer #(.select(3), .width(32), .enable("false")) multiplexer_1 (
    .in0(in_3), .in1(in_2), .in2(in_3), .in3(in_1), .in4(in_3), .in5({32{1'b0}}), .in6(in_3),
    .in7({32{1'b0}}), .out(out_5), .sel(in_4[6:4]));

  // Notes on the sheet:
  //   RAM
  //   ROM
  //   REGALU
  //   ALU
endmodule

module CLOCK (
  input  [7:0] INS,
  output CL
);

  wire clock_1_out, comparator_1_eq, d_ff_1_q, not_1_out;

  Clock clock_1 (.out(clock_1_out));
  Comparator comparator_1 (.a(INS), .b({8{1'b1}}), .eq(comparator_1_eq));  // open: gt, lt
  and and_1 (CL, clock_1_out, not_1_out);
  D_Flip_Flop d_ff_1 (.clk(clock_1_out), .D(comparator_1_eq), .Q(d_ff_1_q));  // open: Qn, preset, en, reset
  not not_1 (not_1_out, d_ff_1_q);
endmodule
